// Logisim project Computer8Bit.circ as structural Verilog: 17 circuits, main circuit main
module main (
);

  wire C1, C2, C3, C4, J, JA, JC, JN, JZ, not_1_out, not_2_out, not_3_out, not_4_out, not_5_out, NOT_ABH_IN,
       NOT_ABL_IN, NOT_CS_IN, NOT_CS_OUT, NOT_DATA_LATCH_OUT, NOT_DEVICE_IN, NOT_DEVICE_OUT,
       NOT_DEVICE_SEL_RAM, NOT_DEVICE_SEL_ROM, NOT_FETCH, NOT_FI, NOT_FLAGS_RS, NOT_HLT, NOT_PASS, NOT_PC_IN,
       NOT_PC_INC, NOT_PC_OUT, NOT_POP, NOT_PUSH, NOT_RA_IN, NOT_RA_OUT, NOT_RA_SL, NOT_RA_SR, NOT_RB_IN,
       NOT_RB_OUT, NOT_RC_IN, NOT_RC_OUT, NOT_RD_IN, NOT_RD_OUT, NOT_RT_IN, NOT_RT_OUT, NOT_SP_CT, NOT_SP_IN,
       NOT_SS_IN, OP_SEL0, OP_SEL1, OP_SEL2, PAGE_0, RESET, ROM_AS, SP_DIR, switch_1_p2, X_SEL0, X_SEL1,
       Y_SEL0, Y_SEL1;
  wire [2:0] alu_1_flags;
  wire [3:0] flagsregister_1_flags_out;
  wire [7:0] ABH_q, aluoperandselector_1_o1, aluoperandselector_1_o2, aluoperatorselector_1_op_out,
       DATA_LATCH_q, DBUS, RA_async_out, RB_async_out, RC_async_out, RD_async_out, rommodule_1_ir_out,
       SP_sp_out, SS_q, undriven;
  wire [12:0] codesegment_programcounter_1_cs_pc;
  wire [15:0] ABUS;

  // DipSwitch dipswitch_1: pin names not known
  assign DBUS = switch_1_p2 ? undriven : 8'bz;  // Controlled_Buffer controlled_buffer_1
  // Switch switch_1: pin names not known; wires that end beside it: 1'b1, switch_1_p2
  Pull_Resistor pull_resistor_1 (.node(switch_1_p2));
  Hex_Digit_Display hex_digit_display_1 (.value(DBUS[7:4]));  // open: dp
  Hex_Digit_Display hex_digit_display_2 (.value(DBUS[3:0]));  // open: dp
  LED led_1 (.in(NOT_RA_IN));
  ControlUnit controlunit_1 (
    .DATA_LATCH(DATA_LATCH_q), .CLK90(C1), .RESET(RESET), .NOT_RA_IN(NOT_RA_IN), .NOT_RA_OUT(NOT_RA_OUT),
    .NOT_RA_SL(NOT_RA_SL), .NOT_RA_SR(NOT_RA_SR), .NOT_RB_IN(NOT_RB_IN), .NOT_RB_OUT(NOT_RB_OUT),
    .NOT_RC_IN(NOT_RC_IN), .NOT_RC_OUT(NOT_RC_OUT), .NOT_RD_IN(NOT_RD_IN), .NOT_RD_OUT(NOT_RD_OUT),
    .NOT_DEVICE_IN(NOT_DEVICE_IN), .NOT_DEVICE_OUT(NOT_DEVICE_OUT), .NOT_SS_IN(NOT_SS_IN),
    .NOT_SP_IN(NOT_SP_IN), .NOT_SP_CT(NOT_SP_CT), .SP_DIR(SP_DIR), .NOT_ABH_IN(NOT_ABH_IN),
    .NOT_ABL_IN(NOT_ABL_IN), .NOT_RT_IN(NOT_RT_IN), .NOT_RT_OUT(NOT_RT_OUT), .X_SEL0(X_SEL0),
    .X_SEL1(X_SEL1), .Y_SEL0(Y_SEL0), .Y_SEL1(Y_SEL1), .OP_SEL0(OP_SEL0), .OP_SEL1(OP_SEL1),
    .OP_SEL2(OP_SEL2), .ROM_AS(ROM_AS), .NOT_CS_IN(NOT_CS_IN), .NOT_PC_IN(NOT_PC_IN),
    .NOT_PC_INC(NOT_PC_INC), .NOT_CS_OUT(NOT_CS_OUT), .NOT_PC_OUT(NOT_PC_OUT), .NOT_FETCH(NOT_FETCH),
    .NOT_FI(NOT_FI), .NOT_FLAGS_RS(NOT_FLAGS_RS), .J(J), .JC(JC), .JZ(JZ), .JN(JN), .JA(JA),
    .NOT_PASS(NOT_PASS), .NOT_HLT(NOT_HLT), .PAGE_0(PAGE_0), .NOT_PUSH(NOT_PUSH), .NOT_POP(NOT_POP),
    .NOT_DATA_LATCH_OUT(NOT_DATA_LATCH_OUT));
  LED led_2 (.in(NOT_RA_OUT));
  LED led_3 (.in(NOT_RA_SL));
  LED led_4 (.in(NOT_RA_SR));
  LED led_5 (.in(NOT_RB_IN));
  LED led_6 (.in(NOT_RB_OUT));
  LED led_7 (.in(NOT_RC_IN));
  LED led_8 (.in(NOT_RC_OUT));
  LED led_9 (.in(NOT_RD_IN));
  LED led_10 (.in(NOT_RD_OUT));
  LED led_11 (.in(NOT_DEVICE_IN));
  LED led_12 (.in(NOT_DEVICE_OUT));
  LED led_13 (.in(NOT_SS_IN));
  LED led_14 (.in(NOT_SP_IN));
  LED led_15 (.in(NOT_SP_CT));
  LED led_16 (.in(SP_DIR));
  LED led_17 (.in(NOT_ABH_IN));
  LED led_18 (.in(NOT_ABL_IN));
  LED led_19 (.in(NOT_RT_IN));
  LED led_20 (.in(NOT_RT_OUT));
  LED led_21 (.in(X_SEL0));
  LED led_22 (.in(X_SEL1));
  LED led_23 (.in(Y_SEL0));
  LED led_24 (.in(Y_SEL1));
  LED led_25 (.in(OP_SEL0));
  LED led_26 (.in(OP_SEL1));
  LED led_27 (.in(OP_SEL2));
  LED led_28 (.in(ROM_AS));
  LED led_29 (.in(NOT_CS_IN));
  LED led_30 (.in(NOT_PC_IN));
  LED led_31 (.in(NOT_PC_INC));
  LED led_32 (.in(NOT_CS_OUT));
  LED led_33 (.in(NOT_PC_OUT));
  LED led_34 (.in(NOT_FETCH));
  LED led_35 (.in(NOT_FI));
  LED led_36 (.in(NOT_FLAGS_RS));
  LED led_37 (.in(J));
  LED led_38 (.in(JC));
  LED led_39 (.in(JZ));
  LED led_40 (.in(JN));
  LED led_41 (.in(JA));
  LED led_42 (.in(NOT_PASS));
  LED led_43 (.in(NOT_HLT));
  LED led_44 (.in(PAGE_0));
  LED led_45 (.in(NOT_PUSH));
  LED led_46 (.in(NOT_POP));
  LED led_47 (.in(NOT_DATA_LATCH_OUT));
  Hex_Digit_Display hex_digit_display_3 (.value(ABUS[15:12]));  // open: dp
  Hex_Digit_Display hex_digit_display_4 (.value(ABUS[11:8]));  // open: dp
  Hex_Digit_Display hex_digit_display_5 (.value(ABUS[7:4]));  // open: dp
  Hex_Digit_Display hex_digit_display_6 (.value(ABUS[3:0]));  // open: dp
  Pull_Resistor pull_resistor_2 (.node(RESET));
  // Switch RESET: pin names not known; wires that end beside it: 1'b1, RESET
  Register ABH (.D(DBUS), .en(not_1_out), .clk(C4), .Q(ABH_q));  // open: clr
  not not_1 (not_1_out, NOT_ABH_IN);
  Register SS (.D(DBUS), .en(not_2_out), .clk(C4), .Q(SS_q), .clr(1'b0));
  not not_2 (not_2_out, NOT_SS_IN);
  Register ABL (.D(DBUS), .en(not_3_out), .clk(C4), .Q(ABUS[7:0]));  // open: clr
  not not_3 (not_3_out, NOT_ABL_IN);
  Multiplexer #(.width(8)) multiplexer_1 (.in0(ABH_q), .in1(8'h20), .out(ABUS[15:8]), .sel(PAGE_0));
  AddrDecoder addrdecoder_1 (
    .ABUS(ABUS), .NOT_DEVICE_SEL_ROM(NOT_DEVICE_SEL_ROM), .NOT_DEVICE_SEL_RAM(NOT_DEVICE_SEL_RAM));
  StackPointer SP (.NOT_SP_IN(NOT_SP_IN), .SP_DIR(SP_DIR), .NOT_SP_CT(NOT_SP_CT), .CLK(C4), .SP_OUT(SP_sp_out));
  CodeSegment_ProgramCounter codesegment_programcounter_1 (
    .FLAGS(flagsregister_1_flags_out), .J(J), .JC(JC), .JZ(JZ), .JN(JN), .JA(JA), .NOT_PC_IN(NOT_PC_IN),
    .NOT_CS_IN(NOT_CS_IN), .NOT_PC_INC(NOT_PC_INC), .RESET(RESET), .ABUS(ABUS), .CLK(C3),
    .NOT_PC_OUT(NOT_PC_OUT), .NOT_CS_OUT(NOT_CS_OUT), .CS_PC(codesegment_programcounter_1_cs_pc),
    .BUS_OUT(DBUS));
  Register DATA_LATCH (.D(rommodule_1_ir_out), .en(not_4_out), .clk(C2), .Q(DATA_LATCH_q), .clr(RESET));
  not not_4 (not_4_out, NOT_FETCH);
  not not_5 (not_5_out, NOT_DATA_LATCH_OUT);
  assign DBUS = not_5_out ? DATA_LATCH_q : 8'bz;  // Controlled_Buffer controlled_buffer_2
  BufferedRegister bufferedregister_1 (
    .BUS_IN(DBUS), .CLK(C4), .NOT_R_IN(NOT_RT_IN), .NOT_R_OUT(NOT_RT_OUT), .BUS_OUT(DBUS));  // open: ASYNC_OUT
  ClockModule clockmodule_1 (.NOT_HLT(NOT_HLT), .C2(C2), .C1(C1), .C4(C4), .C3(C3));
  RAMModule rammodule_1 (
    .NOT_PUSH(NOT_PUSH), .NOT_DEVICE_IN(NOT_DEVICE_IN), .BUS_IN(DBUS),
    .NOT_DEVICE_SEL_RAM(NOT_DEVICE_SEL_RAM), .SP(SP_sp_out), .NOT_DEVICE_OUT(NOT_DEVICE_OUT),
    .NOT_POP(NOT_POP), .CLK(C4), .SS(SS_q), .ABUS(ABUS), .BUS_OUT(DBUS));
  ROMModule rommodule_1 (
    .ABUS(ABUS), .CS_PC(codesegment_programcounter_1_cs_pc), .ROM_AS(ROM_AS), .CLK(C3),
    .NOT_DEVICE_SEL_ROM(NOT_DEVICE_SEL_ROM), .NOT_DEVICE_OUT(NOT_DEVICE_OUT), .NOT_FETCH(NOT_FETCH),
    .BUS_OUT(DBUS), .IR_OUT(rommodule_1_ir_out));
  BufferedRegister RC (
    .BUS_IN(DBUS), .CLK(C4), .NOT_R_IN(NOT_RC_IN), .NOT_R_OUT(NOT_RC_OUT), .ASYNC_OUT(RC_async_out),
    .BUS_OUT(DBUS));
  Hex_Digit_Display hex_digit_display_7 (.value(RC_async_out[7:4]));  // open: dp
  ShiftRegister RA (
    .NOT_SR(NOT_RA_SR), .NOT_IE(NOT_RA_IN), .NOT_SL(NOT_RA_SL), .CLK(C4), .BUS_IN(DBUS), .NOT_OE(NOT_RA_OUT),
    .ASYNC_OUT(RA_async_out), .BUS_OUT(DBUS));
  Hex_Digit_Display hex_digit_display_8 (.value(RA_async_out[7:4]));  // open: dp
  Hex_Digit_Display hex_digit_display_9 (.value(RC_async_out[3:0]));  // open: dp
  Hex_Digit_Display hex_digit_display_10 (.value(RA_async_out[3:0]));  // open: dp
  ALUOperandSelector aluoperandselector_1 (
    .X_SEL0(X_SEL0), .X_SEL1(X_SEL1), .Y_SEL0(Y_SEL0), .Y_SEL1(Y_SEL1), .A_ASYNC(RA_async_out),
    .B_ASYNC(RB_async_out), .C_ASYNC(RC_async_out), .D_ASYNC(RD_async_out), .O1(aluoperandselector_1_o1),
    .O2(aluoperandselector_1_o2));
  BufferedRegister RD (
    .BUS_IN(DBUS), .CLK(C4), .NOT_R_IN(NOT_RD_IN), .NOT_R_OUT(NOT_RD_OUT), .ASYNC_OUT(RD_async_out),
    .BUS_OUT(DBUS));
  BufferedRegister RB (
    .BUS_IN(DBUS), .CLK(C4), .NOT_R_IN(NOT_RB_IN), .NOT_R_OUT(NOT_RB_OUT), .ASYNC_OUT(RB_async_out),
    .BUS_OUT(DBUS));
  Hex_Digit_Display hex_digit_display_11 (.value(RB_async_out[7:4]));  // open: dp
  Hex_Digit_Display hex_digit_display_12 (.value(RD_async_out[7:4]));  // open: dp
  Hex_Digit_Display hex_digit_display_13 (.value(RD_async_out[3:0]));  // open: dp
  Hex_Digit_Display hex_digit_display_14 (.value(RB_async_out[3:0]));  // open: dp
  ALUOperatorSelector aluoperatorselector_1 (
    .OP_SEL0(OP_SEL0), .OP_SEL1(OP_SEL1), .OP_SEL2(OP_SEL2), .OP_OUT(aluoperatorselector_1_op_out));
  ALU alu_1 (
    .OPERATORS(aluoperatorselector_1_op_out), .O1(aluoperandselector_1_o1), .O2(aluoperandselector_1_o2),
    .BUS_OUT(DBUS), .FLAGS(alu_1_flags));
  FLAGSRegister flagsregister_1 (
    .ALU_FLAGS(alu_1_flags), .NOT_FI(NOT_FI), .CLK(C4), .NOT_FLAGS_RS(NOT_FLAGS_RS),
    .FLAGS_OUT(flagsregister_1_flags_out));
  LED led_48 (.in(flagsregister_1_flags_out[3]));
  LED led_49 (.in(flagsregister_1_flags_out[2]));
  LED led_50 (.in(flagsregister_1_flags_out[1]));
  LED led_51 (.in(flagsregister_1_flags_out[0]));

  // Notes on the sheet:
  //   Write to bus
  //   Data bus
  //   Address bus
  //   1. control 2. fetch 3. PC increment 4. data
  //   ROM
  //   Clock
  //   RAM
  //   DATA_LATCH
  //   RT
  //   RC
  //   RA
  //   ALU_OPERAND_SELECTOR
  //   RD
  //   RB
  //   ALU_OPERATOR_SELECTOR
  //   A
  //   N
  //   Z
  //   C
endmodule

module ShiftRegister (
  input  NOT_SR,
  input  NOT_IE,
  input  NOT_SL,
  input  CLK,
  input  [7:0] BUS_IN,
  input  NOT_OE,
  output [7:0] ASYNC_OUT,
  output [7:0] BUS_OUT
);

  wire not_1_out, S0_out, S1_out;

  not not_1 (not_1_out, NOT_OE);
  nand S0 (S0_out, NOT_SR, NOT_IE);
  nand S1 (S1_out, NOT_IE, NOT_SL);
  L_8_bit_universal_shift_storage_register_with_3_state_outputs_SN74ALS299_87cfe9f2 l_8_bit_universal_shift_storage_register_with_3_state_outputs_sn74als299_87cfe9f2_1 (
    .CLK(CLK), .NOT_CLR(1'b1), .NOT_OE1(1'b0), .NOT_OE2(1'b0), .BUS_IN(BUS_IN), .S1(S1_out), .SR(1'b0),
    .S0(S0_out), .SL(1'b0), .BUS_OUT(ASYNC_OUT));  // open: QA1, QH1
  assign BUS_OUT = not_1_out ? ASYNC_OUT : 8'bz;  // Controlled_Buffer controlled_buffer_1
endmodule

module BufferedRegister (
  input  [7:0] BUS_IN,
  input  CLK,
  input  NOT_R_IN,
  input  NOT_R_OUT,
  output [7:0] ASYNC_OUT,
  output [7:0] BUS_OUT
);

  wire not_1_out, not_2_out;

  not not_1 (not_1_out, NOT_R_IN);
  not not_2 (not_2_out, NOT_R_OUT);
  Register register_1 (.D(BUS_IN), .en(not_1_out), .clk(CLK), .Q(ASYNC_OUT), .clr(1'b0));
  assign BUS_OUT = not_2_out ? ASYNC_OUT : 8'bz;  // Controlled_Buffer controlled_buffer_1
endmodule

module ALUOperandSelector (
  input  X_SEL0,
  input  X_SEL1,
  input  Y_SEL0,
  input  Y_SEL1,
  input  [7:0] A_ASYNC,
  input  [7:0] B_ASYNC,
  input  [7:0] C_ASYNC,
  input  [7:0] D_ASYNC,
  output [7:0] O1,
  output [7:0] O2
);

  wire decoder_1_out0, decoder_1_out1, decoder_1_out2, decoder_1_out3, decoder_2_out0, decoder_2_out1,
       decoder_2_out2, decoder_2_out3;

  Decoder #(.select(2)) decoder_1 (
    .out0(decoder_1_out0), .out1(decoder_1_out1), .out2(decoder_1_out2), .out3(decoder_1_out3),
    .sel({X_SEL1, X_SEL0}), .en(1'b1));
  Decoder #(.select(2)) decoder_2 (
    .out0(decoder_2_out0), .out1(decoder_2_out1), .out2(decoder_2_out2), .out3(decoder_2_out3),
    .sel({Y_SEL1, Y_SEL0}), .en(1'b1));
  assign O1 = decoder_1_out0 ? A_ASYNC : 8'bz;  // Controlled_Buffer controlled_buffer_1
  assign O1 = decoder_1_out1 ? B_ASYNC : 8'bz;  // Controlled_Buffer controlled_buffer_2
  assign O1 = decoder_1_out2 ? C_ASYNC : 8'bz;  // Controlled_Buffer controlled_buffer_3
  assign O1 = decoder_1_out3 ? D_ASYNC : 8'bz;  // Controlled_Buffer controlled_buffer_4
  assign O2 = decoder_2_out0 ? A_ASYNC : 8'bz;  // Controlled_Buffer controlled_buffer_5
  assign O2 = decoder_2_out1 ? B_ASYNC : 8'bz;  // Controlled_Buffer controlled_buffer_6
  assign O2 = decoder_2_out2 ? C_ASYNC : 8'bz;  // Controlled_Buffer controlled_buffer_7
  assign O2 = decoder_2_out3 ? D_ASYNC : 8'bz;  // Controlled_Buffer controlled_buffer_8
endmodule

module ALUOperatorSelector (
  input  OP_SEL0,
  input  OP_SEL1,
  input  OP_SEL2,
  output [7:0] OP_OUT
);

  Decoder #(.select(3)) decoder_1 (
    .out0(OP_OUT[0]), .out1(OP_OUT[1]), .out2(OP_OUT[2]), .out3(OP_OUT[3]), .out4(OP_OUT[4]),
    .out5(OP_OUT[5]), .out6(OP_OUT[6]), .out7(OP_OUT[7]), .sel({OP_SEL2, OP_SEL1, OP_SEL0}), .en(1'b1));
endmodule

module ALU (
  input  [7:0] OPERATORS,
  input  [7:0] O1,
  input  [7:0] O2,
  output [7:0] BUS_OUT,
  output [2:0] FLAGS
);

  wire and_2_out, and_3_out, nor_1_out, nor_2_out, nor_3_out, nor_4_out, or_2_out;
  wire [6:0] buffer_1_out;
  wire [7:0] adder_1_out, and_1_out, bit_extender_1_out, not_1_out, or_1_out, xor_1_out, xor_2_out;

  assign not_1_out = ~O1;  // NOT_Gate not_1, 8 bits wide
  assign xor_1_out = O1 ^ O2;  // XOR_Gate xor_1, 8 bits wide
  assign BUS_OUT = OPERATORS[6] ? not_1_out : 8'bz;  // Controlled_Buffer controlled_buffer_1
  assign BUS_OUT = OPERATORS[5] ? xor_1_out : 8'bz;  // Controlled_Buffer controlled_buffer_2
  assign and_1_out = O1 & O2;  // AND_Gate and_1, 8 bits wide
  assign BUS_OUT = OPERATORS[4] ? and_1_out : 8'bz;  // Controlled_Buffer controlled_buffer_3
  // NoConnect on OPERATORS[7]
  assign or_1_out = O1 | O2;  // OR_Gate or_1, 8 bits wide
  assign BUS_OUT = OPERATORS[3] ? or_1_out : 8'bz;  // Controlled_Buffer controlled_buffer_4
  nor nor_1 (nor_1_out, FLAGS[2], buffer_1_out[6]);
  assign bit_extender_1_out = {{7{OPERATORS[2]}}, OPERATORS[2]};  // Bit_Extender bit_extender_1
  assign {FLAGS[2], buffer_1_out} = BUS_OUT;  // Buffer buffer_1, 8 bits wide
  Pull_Resistor pull_resistor_1 (.node({FLAGS[2], buffer_1_out}));
  nor nor_2 (nor_2_out, buffer_1_out[5], buffer_1_out[4]);
  nor nor_3 (nor_3_out, buffer_1_out[3], buffer_1_out[2]);
  and and_2 (and_2_out, nor_1_out, nor_2_out);
  and and_3 (and_3_out, nor_3_out, nor_4_out);
  and and_4 (FLAGS[1], and_2_out, and_3_out);
  Adder adder_1 (.a(O1), .b(xor_2_out), .out(adder_1_out), .cin(OPERATORS[2]), .cout(FLAGS[0]));
  assign xor_2_out = O2 ^ bit_extender_1_out;  // XOR_Gate xor_2, 8 bits wide
  assign BUS_OUT = or_2_out ? adder_1_out : 8'bz;  // Controlled_Buffer controlled_buffer_5
  nor nor_4 (nor_4_out, buffer_1_out[1], buffer_1_out[0]);
  or or_2 (or_2_out, OPERATORS[2], OPERATORS[1]);
endmodule

module FLAGSRegister (
  input  [2:0] ALU_FLAGS,
  input  NOT_FI,
  input  CLK,
  input  NOT_FLAGS_RS,
  output [3:0] FLAGS_OUT
);

  wire not_1_out, not_2_out;

  Register #(.width(4)) register_1 (.D({1'b0, ALU_FLAGS}), .en(not_1_out), .clk(CLK), .Q(FLAGS_OUT), .clr(not_2_out));
  not not_1 (not_1_out, NOT_FI);
  not not_2 (not_2_out, NOT_FLAGS_RS);
endmodule

module ClockModule (
  input  NOT_HLT,
  output C2,
  output C1,
  output C4,
  output C3
);

  wire CLK90_GEN_out, CLK_GEN_out;

  Clock #(.highDuration(2), .lowDuration(2), .phaseOffset(3)) CLK_GEN (.out(CLK_GEN_out));
  Clock #(.highDuration(2), .lowDuration(2)) CLK90_GEN (.out(CLK90_GEN_out));
  and and_1 (C2, CLK_GEN_out, NOT_HLT);
  and and_2 (C1, NOT_HLT, CLK90_GEN_out);
  not not_1 (C4, C2);
  not not_2 (C3, C1);
endmodule

module InstructionRegister (
);

  Counter counter_1 ();  // open: clr, load, up, count, clk, D, carry, Q
endmodule

module RAMModule (
  input  NOT_PUSH,
  input  NOT_DEVICE_IN,
  input  [7:0] BUS_IN,
  input  NOT_DEVICE_SEL_RAM,
  input  [7:0] SP,
  input  NOT_DEVICE_OUT,
  input  NOT_POP,
  input  CLK,
  input  [7:0] SS,
  input  [15:0] ABUS,
  output [7:0] BUS_OUT
);

  wire nand_1_out, nand_2_out, nand_3_out, nand_4_out, nand_5_out, nand_6_out, nand_7_out, not_1_out,
       not_2_out;
  wire [7:0] multiplexer_1_out, multiplexer_2_out, ram_1_data;

  Multiplexer #(.width(8)) multiplexer_1 (.in0(ABUS[7:0]), .in1(SP), .out(multiplexer_1_out), .sel(nand_1_out));
  Multiplexer #(.width(8)) multiplexer_2 (
    .in0({3'b000, ABUS[12:8]}), .in1(SS), .out(multiplexer_2_out), .sel(nand_1_out));
  RAM #(.addrWidth(13), .asyncread("true"), .databus("bidir")) ram_1 (
    .addr({multiplexer_2_out[4:0], multiplexer_1_out}), .we(not_1_out), .oe(not_2_out), .clk(CLK),
    .data(ram_1_data));
  nand nand_1 (nand_1_out, NOT_PUSH, NOT_POP);
  not not_1 (not_1_out, nand_2_out);
  assign ram_1_data = not_1_out ? BUS_IN : 8'bz;  // Controlled_Buffer controlled_buffer_1
  nand nand_2 (nand_2_out, nand_4_out, nand_5_out);
  not not_2 (not_2_out, nand_3_out);
  nand nand_3 (nand_3_out, nand_6_out, nand_7_out);
  assign BUS_OUT = not_2_out ? ram_1_data : 8'bz;  // Controlled_Buffer controlled_buffer_2
  nand nand_4 (nand_4_out, NOT_PUSH, NOT_DEVICE_IN);
  nand nand_5 (nand_5_out, NOT_DEVICE_SEL_RAM, NOT_PUSH);
  nand nand_6 (nand_6_out, NOT_DEVICE_SEL_RAM, NOT_POP);
  nand nand_7 (nand_7_out, NOT_DEVICE_OUT, NOT_POP);
endmodule

module StackPointer (
  input  NOT_SP_IN,
  input  SP_DIR,
  input  NOT_SP_CT,
  input  CLK,
  output [7:0] SP_OUT
);

  wire not_1_out, not_2_out;

  not not_1 (not_1_out, NOT_SP_IN);
  Counter counter_1 (
    .clr(1'b0), .load(not_1_out), .up(SP_DIR), .count(not_2_out), .clk(CLK), .D({8{1'b0}}), .Q(SP_OUT));  // open: carry
  not not_2 (not_2_out, NOT_SP_CT);
endmodule

module ROMModule (
  input  [15:0] ABUS,
  input  [12:0] CS_PC,
  input  ROM_AS,
  input  CLK,
  input  NOT_DEVICE_SEL_ROM,
  input  NOT_DEVICE_OUT,
  input  NOT_FETCH,
  output [7:0] BUS_OUT,
  output [7:0] IR_OUT
);

  wire nand_1_out, nand_2_out, not_1_out, not_2_out, or_1_out;
  wire [7:0] STORAGE_ROM_data;
  wire [12:0] multiplexer_1_out;

  nand nand_1 (nand_1_out, ROM_AS, 1'b1);
  Multiplexer #(.width(13)) multiplexer_1 (.in0(ABUS[12:0]), .in1(CS_PC), .out(multiplexer_1_out), .sel(nand_2_out));
  nand nand_2 (nand_2_out, CLK, nand_1_out);
  ROM #(.addrWidth(13)) STORAGE_ROM (.addr(multiplexer_1_out), .data(STORAGE_ROM_data));
  not not_1 (not_1_out, or_1_out);
  or or_1 (or_1_out, NOT_DEVICE_SEL_ROM, NOT_DEVICE_OUT);
  assign BUS_OUT = not_1_out ? STORAGE_ROM_data : 8'bz;  // Controlled_Buffer controlled_buffer_1
  assign IR_OUT = not_2_out ? STORAGE_ROM_data : 8'bz;  // Controlled_Buffer controlled_buffer_2
  not not_2 (not_2_out, NOT_FETCH);

  // Notes on the sheet:
  //   This way we ensure that ROM_AS is 1 during data latch (consult timing diagram)
  //   contents of STORAGE_ROM (hex, n*v repeats v):
  //   5 0 4 1 3 ff 2c 1f 1f 64 83 be 10 bf 6 0 1 7919*0 1 2 3 4 5 6 7 8 9 a b c d e f 10 11 12 13 14 15 16
  //   17 18 19 1a 1b 1c 1d 1e 1f 20 21 22 23 24 25 26 27 28 29 2a 2b 2c 2d 2e 2f 30 31 32 33 34 35 36 37
  //   38 39 3a 3b 3c 3d 3e 3f 40 41 42 43 44 45 46 47 48 49 4a 4b 4c 4d 4e 4f 50 51 52 53 54 55 56 57 58
  //   59 5a 5b 5c 5d 5e 5f 60 61 62 63 64 65 66 67 68 69 6a 6b 6c 6d 6e 6f 70 71 72 73 74 75 76 77 78 79
  //   7a 7b 7c 7d 7e 7f 80 81 82 83 84 85 86 87 88 89 8a 8b 8c 8d 8e 8f 90 91 92 93 94 95 96 97 98 99 9a
  //   9b 9c 9d 9e 9f a0 a1 a2 a3 a4 a5 a6 a7 a8 a9 aa ab ac ad ae af b0 b1 b2 b3 b4 b5 b6 b7 b8 b9 ba bb
  //   bc bd be bf c0 c1 c2 c3 c4 c5 c6 c7 c8 c9 ca cb cc cd ce cf d0 d1 d2 d3 d4 d5 d6 d7 d8 d9 da db dc
  //   dd de df e0 e1 e2 e3 e4 e5 e6 e7 e8 e9 ea eb ec ed ee ef f0 f1 f2 f3 f4 f5 f6 f7 f8 f9 fa fb fc fd
  //   fe ff
endmodule

module CodeSegment_ProgramCounter (
  input  [3:0] FLAGS,
  input  J,
  input  JC,
  input  JZ,
  input  JN,
  input  JA,
  input  NOT_PC_IN,
  input  NOT_CS_IN,
  input  NOT_PC_INC,
  input  RESET,
  input  [15:0] ABUS,
  input  CLK,
  input  NOT_PC_OUT,
  input  NOT_CS_OUT,
  output [12:0] CS_PC,
  output [7:0] BUS_OUT
);

  wire and_1_out, and_2_out, and_3_out, and_4_out, and_5_out, nor_1_out, nor_2_out, nor_3_out, not_1_out,
       not_2_out, not_3_out, or_1_out, or_2_out, or_3_out, or_4_out, PC_carry;
  wire [7:5] CS_q;

  and and_1 (and_1_out, JC, FLAGS[0]);
  or or_1 (or_1_out, and_1_out, and_2_out);
  and and_2 (and_2_out, JZ, FLAGS[1]);
  and and_3 (and_3_out, JN, FLAGS[2]);
  or or_2 (or_2_out, and_3_out, and_4_out);
  or or_3 (or_3_out, or_1_out, or_2_out);
  nor nor_1 (nor_1_out, J, or_3_out);
  and and_4 (and_4_out, JA, FLAGS[3]);
  nor nor_2 (nor_2_out, NOT_CS_IN, nor_1_out);
  and and_5 (and_5_out, CLK, or_4_out);
  or or_4 (or_4_out, RESET, CS_q[5]);
  not not_1 (not_1_out, NOT_PC_OUT);
  not not_2 (not_2_out, NOT_CS_OUT);
  Counter CS (
    .clr(and_5_out), .load(nor_2_out), .up(1'b1), .count(PC_carry), .clk(CLK), .D(ABUS[15:8]),
    .Q({CS_q, CS_PC[12:8]}));  // open: carry
  not not_3 (not_3_out, NOT_PC_INC);
  nor nor_3 (nor_3_out, nor_1_out, NOT_PC_IN);
  Counter PC (
    .clr(and_5_out), .load(nor_3_out), .up(1'b1), .count(not_3_out), .clk(CLK), .D(ABUS[7:0]),
    .carry(PC_carry), .Q(CS_PC[7:0]));
  assign BUS_OUT = not_2_out ? {CS_q, CS_PC[12:8]} : 8'bz;  // Controlled_Buffer controlled_buffer_1
  assign BUS_OUT = not_1_out ? CS_PC[7:0] : 8'bz;  // Controlled_Buffer controlled_buffer_2
endmodule

module LCD_emulator (
  input  RS,
  input  R_NW,
  input  LCD_EN,
  input  [7:0] BUS_IN
);
endmodule

module Interface_emulator (
  input  POLL,
  input  TRANSMIT,
  input  CLK,
  input  [7:0] BUS_IN,
  output [7:0] BUS_OUT,
  output A_OUT
);

  wire [7:0] register_1_q;

  Register register_1 (.D(BUS_IN), .en(TRANSMIT), .clk(CLK), .Q(register_1_q));  // open: clr
  assign BUS_OUT = POLL ? register_1_q : 8'bz;  // Controlled_Buffer controlled_buffer_1

  assign A_OUT = POLL;
endmodule

module ControlUnit (
  input  [7:0] DATA_LATCH,
  input  CLK90,
  input  RESET,
  output NOT_RA_IN,
  output NOT_RA_OUT,
  output NOT_RA_SL,
  output NOT_RA_SR,
  output NOT_RB_IN,
  output NOT_RB_OUT,
  output NOT_RC_IN,
  output NOT_RC_OUT,
  output NOT_RD_IN,
  output NOT_RD_OUT,
  output NOT_DEVICE_IN,
  output NOT_DEVICE_OUT,
  output NOT_SS_IN,
  output NOT_SP_IN,
  output NOT_SP_CT,
  output SP_DIR,
  output NOT_ABH_IN,
  output NOT_ABL_IN,
  output NOT_RT_IN,
  output NOT_RT_OUT,
  output X_SEL0,
  output X_SEL1,
  output Y_SEL0,
  output Y_SEL1,
  output OP_SEL0,
  output OP_SEL1,
  output OP_SEL2,
  output ROM_AS,
  output NOT_CS_IN,
  output NOT_PC_IN,
  output NOT_PC_INC,
  output NOT_CS_OUT,
  output NOT_PC_OUT,
  output NOT_FETCH,
  output NOT_FI,
  output NOT_FLAGS_RS,
  output J,
  output JC,
  output JZ,
  output JN,
  output JA,
  output NOT_PASS,
  output NOT_HLT,
  output PAGE_0,
  output NOT_PUSH,
  output NOT_POP,
  output NOT_DATA_LATCH_OUT
);

  wire and_1_out, edgedetector_1_pulse, not_1_out, or_1_out;
  wire [3:0] counter_1_q;
  wire [7:0] EEPROM6_data, IR_q;
  wire [7:7] EEPROM5_data;
  wire [12:0] undriven;

  or or_1 (or_1_out, not_1_out, RESET);
  not not_1 (not_1_out, NOT_PASS);
  Register IR (.D(DATA_LATCH), .en(or_1_out), .clk(CLK90), .Q(IR_q), .clr(RESET));
  EdgeDetector edgedetector_1 (.D(CLK90), .PULSE(edgedetector_1_pulse));
  Counter #(.max('hf), .width(4)) counter_1 (
    .clr(and_1_out), .load(1'b0), .up(1'b1), .count(1'b1), .clk(CLK90), .D(4'b1111), .Q(counter_1_q));  // open: carry
  and and_1 (and_1_out, or_1_out, edgedetector_1_pulse);
  ROM #(.addrWidth(13)) EEPROM0 (
    .addr({1'b0, IR_q, counter_1_q}),
    .data({NOT_RC_OUT, NOT_RC_IN, NOT_RB_OUT, NOT_RB_IN, NOT_RA_SR, NOT_RA_SL, NOT_RA_OUT, NOT_RA_IN}));
  ROM #(.addrWidth(13)) EEPROM1 (
    .addr({1'b0, IR_q, counter_1_q}),
    .data({SP_DIR, NOT_SP_CT, NOT_SP_IN, NOT_SS_IN, NOT_DEVICE_OUT, NOT_DEVICE_IN, NOT_RD_OUT, NOT_RD_IN}));
  ROM #(.addrWidth(13)) EEPROM2 (
    .addr({1'b0, IR_q, counter_1_q}),
    .data({Y_SEL1, Y_SEL0, X_SEL1, X_SEL0, NOT_RT_OUT, NOT_RT_IN, NOT_ABL_IN, NOT_ABH_IN}));
  ROM #(.addrWidth(13)) EEPROM3 (
    .addr({1'b0, IR_q, counter_1_q}),
    .data({NOT_CS_OUT, NOT_PC_INC, NOT_PC_IN, NOT_CS_IN, ROM_AS, OP_SEL2, OP_SEL1, OP_SEL0}));
  ROM #(.addrWidth(13)) EEPROM4 (
    .addr({1'b0, IR_q, counter_1_q}), .data({JN, JZ, JC, J, NOT_FLAGS_RS, NOT_FI, NOT_FETCH, NOT_PC_OUT}));
  ROM #(.addrWidth(13)) EEPROM5 (
    .addr({1'b0, IR_q, counter_1_q}),
    .data({EEPROM5_data[7], NOT_DATA_LATCH_OUT, NOT_POP, NOT_PUSH, PAGE_0, NOT_HLT, NOT_PASS, JA}));
  ROM #(.addrWidth(13)) EEPROM6 (.addr(undriven), .data(EEPROM6_data));

  // Notes on the sheet:
  //   Get the 163! Synchronous reset
  //   contents of EEPROM0 (hex, n*v repeats v):
  //   32*ff fe 15*ff ef 15*ff bf 63*ff ed 15*ff bd 15*ff fd 15*ff de 15*ff 9f 15*ff df 15*ff 7e 15*ff 6f
  //   15*ff 7f 15*ff fe 15*ff ef 15*ff bf 48*ff fd 15*ff df 15*ff 7f 31*ff fe 15*ff ef 15*ff bf 47*ff fd
  //   15*ff df 15*ff 7f 31*ff fe 15*ff ef 15*ff bf 48*ff fd 15*ff df 15*ff 7f 31*ff fe 15*ff ef 15*ff bf
  //   45*ff 7f ff fd 13*ff 7f ff df 13*ff 7f ff 7f 13*ff 7f 15*ff 7f ff fe 13*ff 7f ff ef 13*ff 7f ff bf
  //   13*ff 7f 15*ff 7f 17*ff fd 15*ff df 15*ff 7f 31*ff fe 15*ff ef 15*ff bf 45*ff fd 15*ff df 15*ff 7f
  //   79*ff 7f 48*ff fe 15*ff ef 15*ff bf 78*ff 7f 32*ff fe 15*ff fe 15*ff fe 15*ff fe 14*ff ef 15*ff ef
  //   15*ff ef 15*ff ef 15*ff bf 15*ff bf 15*ff bf 15*ff bf 80*ff fe 15*ff fe 15*ff fe 15*ff fe 14*ff ef
  //   15*ff ef 15*ff ef 15*ff ef 15*ff bf 15*ff bf 15*ff bf 15*ff bf 336*ff fe 15*ff fe 15*ff fe 15*ff fe
  //   14*ff ef 15*ff ef 15*ff ef 15*ff ef 15*ff bf 15*ff bf 15*ff bf 15*ff bf 80*ff fe 15*ff fe 15*ff fe
  //   15*ff fe 14*ff ef 15*ff ef 15*ff ef 15*ff ef 15*ff bf 15*ff bf 15*ff bf 15*ff bf 80*ff fe 15*ff fe
  //   15*ff fe 15*ff fe 14*ff ef 15*ff ef 15*ff ef 15*ff ef 15*ff bf 15*ff bf 15*ff bf 15*ff bf 80*ff fe
  //   14*ff ef 15*ff bf 31*ff fb 15*ff f7 191*ff
  //   contents of EEPROM1 (hex, n*v repeats v):
  //   80*7f 7e 15*7f 7e 15*7f 7e 47*7f 7e 47*7f 7e 47*7f 7e 15*7f 7d 15*7f 7d 15*7f 7d 15*7f 6d 15*7f 5d
  //   16*7f 7b 15*7f 7b 15*7f 7b 15*7f 79 15*7f 77 15*7f 77 15*7f 77 15*7f 76 15*7f 7b 14*7f 7d 7b 14*7f
  //   7d 7b 14*7f 7d 7b 14*7f 7d 79 14*7f 7d 77 14*7f 7d 77 14*7f 7d 77 14*7f 7d 76 14*7f 7d 7b 15*7f 7d
  //   7b 14*7f 7d 7b 14*7f 7d 7b 14*7f 7d 79 14*7f 7d 77 14*7f 7d 77 14*7f 7d 77 14*7f 7d 76 14*7f 7d 7b
  //   14*7f 7d 7b 14*7f 7d 7b 14*7f 7d 7b 14*7f 7d 79 14*7f 7d 77 14*7f 7d 77 14*7f 7d 77 14*7f 7d 76
  //   14*7f 7d 7b 15*7f 7b 15*7f 7b 15*7f 7b 15*7f 79 15*7f 77 15*7f 77 15*7f 77 15*7f 76 15*7f 7b 14*7f
  //   bf 15*7f bf 15*7f bf 14*7f 7d bf 15*7f 77 7f bf 12*7f 7d 77 7f bf 13*7f 7d 77 7f bf 12*7f 7d 77 7f
  //   bf 12*7f 7d 77 7f bf 12*7f bf 14*7f 3f 15*7f 3f 15*7f 3f 15*7f 3f 7e 14*7f 3f 7f 7b 13*7f 3d 7f 7b
  //   14*7f 3d 7f 7b 13*7f 3d 7f 7b 13*7f 3d 7f 7b 204*7f 7e 15*7f 7e 15*7f 7e 15*7f 7e 207*7f 7e 15*7f 7e
  //   15*7f 7e 15*7f 7e 463*7f 7e 15*7f 7e 15*7f 7e 15*7f 7e 207*7f 7e 15*7f 7e 15*7f 7e 15*7f 7e 207*7f
  //   7e 15*7f 7e 15*7f 7e 15*7f 7e 63*7f 7e 176*7f bf bf 13*7f 3f 3f 7f 3f 28*7f
  //   contents of EEPROM2 (hex, n*v repeats v):
  //   352*f d 15*f d 15*f d 15*f d 15*f d 15*f d 15*f d 15*f d 15*f d 15*f d 15*f d 15*f d 15*f d 15*f d
  //   15*f d 15*f d 15*f d 15*f d 15*f e d 14*f e d 14*f e d 14*f e d 14*f e d 14*f e d 14*f e d 14*f e d
  //   14*f e d 14*f e d 14*f e d 14*f e d 14*f e d 14*f e d 14*f e d 14*f e d 14*f e d 14*f e d 14*f e d
  //   14*f e d 14*f e d 14*f e d 14*f e d 14*f e d 14*f e d 14*f e d 14*f e d 78*f d b 7 13*f d b 7 13*f e
  //   d b 7 12*f e d b 7 12*f e d b 7 92*f d b 7 13*f d b 7 13*f e d b 7 12*f e d b 7 12*f e d b 7 12*f b
  //   7 14*f 4b 7 14*f 8b 7 14*f cb 7 14*f 1f 15*f 5f 15*f 9f 15*f df 15*f 2f 15*f 6f 15*f af 15*f ef 15*f
  //   3f 15*f 7f 15*f bf 15*f ff 15*f b 7 14*f 4b 7 14*f 8b 7 14*f cb 7 14*f 1f 15*f 5f 15*f 9f 15*f df
  //   15*f 2f 15*f 6f 15*f af 15*f ef 15*f 3f 15*f 7f 15*f bf 15*f ff 31*f 4f 15*f 8f 15*f cf 15*f 1f 15*f
  //   5f 15*f 9f 15*f df 15*f 2f 15*f 6f 15*f af 15*f ef 15*f 3f 15*f 7f 15*f bf 15*f ff 15*f b 7 14*f 4b
  //   7 14*f 8b 7 14*f cb 7 14*f 1f 15*f 5f 15*f 9f 15*f df 15*f 2f 15*f 6f 15*f af 15*f ef 15*f 3f 15*f
  //   7f 15*f bf 15*f ff 15*f b 7 14*f 4b 7 14*f 8b 7 14*f cb 7 14*f 1f 15*f 5f 15*f 9f 15*f df 15*f 2f
  //   15*f 6f 15*f af 15*f ef 15*f 3f 15*f 7f 15*f bf 15*f ff 15*f b 7 14*f 4b 7 14*f 8b 7 14*f cb 7 14*f
  //   1f 15*f 5f 15*f 9f 15*f df 15*f 2f 15*f 6f 15*f af 15*f ef 15*f 3f 15*f 7f 15*f bf 15*f ff 15*f b 7
  //   14*f 1f 15*f 2f 15*f 3f 47*f d 15*f d 15*f d 15*f d 15*f e d 14*f e d 14*f e d 14*f e d 16*f e d
  //   13*f d e 29*f
  //   contents of EEPROM3 (hex, n*v repeats v):
  //   b0 15*f0 b0 15*f0 b0 b0 14*f0 b0 b0 14*f0 b0 b0 14*f0 b0 b0 14*f0 b0 b0 14*f0 b0 b0 14*f0 b0 15*f0
  //   b0 15*f0 b0 15*f0 b0 15*f0 b0 15*f0 b0 15*f0 b0 15*f0 b0 15*f0 b0 15*f0 b0 15*f0 b0 15*f0 b0 15*f0
  //   b0 15*f0 b0 15*f0 b0 b0 14*f0 b0 b0 14*f0 b0 b0 14*f0 b0 b0 14*f0 b0 b0 14*f0 b0 b0 14*f0 b0 b0
  //   14*f0 b0 b0 14*f0 b0 b0 b0 14*f0 b0 15*f0 b0 15*f0 b0 15*f0 b0 15*f0 b0 15*f0 b0 15*f0 b0 15*f0 b0
  //   15*f0 b0 b0 13*f0 b0 f0 b0 13*f0 b0 f0 b0 13*f0 b0 f0 b0 13*f0 b0 f0 b0 13*f0 b0 f0 b0 13*f0 b0 f0
  //   b0 13*f0 b0 f0 b0 13*f0 b0 f0 b0 13*f0 b0 f0 b0 b0 14*f0 b0 15*f0 b0 15*f0 b0 15*f0 b0 15*f0 b0
  //   15*f0 b0 15*f0 b0 15*f0 b0 15*f0 b0 b0 12*f0 b0 b0 b0 13*f0 b0 b0 b0 13*f0 b0 b0 b0 13*f0 b0 b0 b0
  //   13*f0 b0 b0 b0 13*f0 b0 b0 b0 13*f0 b0 b0 b0 13*f0 b0 b0 b0 13*f0 4*b0 13*f0 b0 15*f0 b0 15*f0 b0
  //   15*f0 b0 14*f0 b0 f0 f0 b0 15*f0 b0 12*f0 b0 f0 f0 f0 b0 15*f0 b0 11*f0 b0 f0 f0 f0 b0 11*f0 b0 b0
  //   15*f0 b0 15*f0 b0 15*f0 b0 15*f0 b0 14*f0 b0 f0 b0 15*f0 b0 13*f0 b0 f0 f0 b0 15*f0 b0 12*f0 b0 f0
  //   f0 b0 12*f0 f1 b0 14*f0 f1 b0 14*f0 f1 b0 14*f0 f1 b0 14*f0 b1 15*f0 b1 15*f0 b1 15*f0 b1 15*f0 b1
  //   15*f0 b1 15*f0 b1 15*f0 b1 15*f0 b1 15*f0 b1 15*f0 b1 15*f0 b1 15*f0 f2 b0 14*f0 f2 b0 14*f0 f2 b0
  //   14*f0 f2 b0 14*f0 b2 15*f0 b2 15*f0 b2 15*f0 b2 15*f0 b2 15*f0 b2 15*f0 b2 15*f0 b2 15*f0 b2 15*f0
  //   b2 15*f0 b2 15*f0 b2 15*f0 b2 15*f0 b2 15*f0 b2 15*f0 b2 15*f0 b2 15*f0 b2 15*f0 b2 15*f0 b2 15*f0
  //   b2 15*f0 b2 15*f0 b2 15*f0 b2 15*f0 b2 15*f0 b2 15*f0 b2 15*f0 b2 15*f0 f3 b0 14*f0 f3 b0 14*f0 f3
  //   b0 14*f0 f3 b0 14*f0 b3 15*f0 b3 15*f0 b3 15*f0 b3 15*f0 b3 15*f0 b3 15*f0 b3 15*f0 b3 15*f0 b3
  //   15*f0 b3 15*f0 b3 15*f0 b3 15*f0 f4 b0 14*f0 f4 b0 14*f0 f4 b0 14*f0 f4 b0 14*f0 b4 15*f0 b4 15*f0
  //   b4 15*f0 b4 15*f0 b4 15*f0 b4 15*f0 b4 15*f0 b4 15*f0 b4 15*f0 b4 15*f0 b4 15*f0 b4 15*f0 f5 b0
  //   14*f0 f5 b0 14*f0 f5 b0 14*f0 f5 b0 14*f0 b5 15*f0 b5 15*f0 b5 15*f0 b5 15*f0 b5 15*f0 b5 15*f0 b5
  //   15*f0 b5 15*f0 b5 15*f0 b5 15*f0 b5 15*f0 b5 15*f0 f6 b0 14*f0 b6 15*f0 b6 15*f0 b6 15*f0 b0 15*f0
  //   b0 15*f0 b0 d0 b0 13*f0 b0 d0 b0 13*f0 b0 d0 b0 13*f0 b0 d0 b0 13*f0 b0 b0 c0 b0 12*f0 b0 b0 c0 b0
  //   12*f0 b0 b0 c0 b0 12*f0 b0 b0 c0 b0 12*f0 70 f0 b0 b0 c0 b0 13*f0 c0 b0 11*f0 b0 15*f0
  //   contents of EEPROM4 (hex, n*v repeats v):
  //   d 15*f d 15*f d d 14*f d d 14*f d d 14*f d d 14*f d d 14*f d d 14*f d 15*f d 15*f d 15*f d 15*f d
  //   15*f d 15*f d 15*f d 15*f d 15*f d 15*f d 15*f d 15*f d 15*f d 15*f d d 14*f d d 14*f d d 14*f d d
  //   14*f d d 14*f d d 14*f d d 14*f d d 14*f d d d 14*f d 15*f d 15*f d 15*f d 15*f d 15*f d 15*f d 15*f
  //   d 15*f d d 13*f d f d 13*f d f d 13*f d f d 13*f d f d 13*f d f d 13*f d f d 13*f d f d 13*f d f d
  //   13*f d f d d 14*f d 15*f d 15*f d 15*f d 15*f d 15*f d 15*f d 15*f d 15*f d d 12*f d d d 13*f d d d
  //   13*f d d d 13*f d d d 13*f d d d 13*f d d d 13*f d d d 13*f d d d 13*f 4*d 13*f d 15*f d 15*f d 15*f
  //   d 14*f d f f d 15*f d 12*f d f f f d 15*f d 11*f d f f f d 11*f d d 15*f d 15*f d 15*f d 15*f d 14*f
  //   d f d 15*f d 13*f d f f d 15*f d 12*f d f f d 12*f b d 14*f b d 14*f b d 14*f b d 14*f 9 15*f 9 15*f
  //   9 15*f 9 15*f 9 15*f 9 15*f 9 15*f 9 15*f 9 15*f 9 15*f 9 15*f 9 15*f b d 14*f b d 14*f b d 14*f b d
  //   14*f 9 15*f 9 15*f 9 15*f 9 15*f 9 15*f 9 15*f 9 15*f 9 15*f 9 15*f 9 15*f 9 15*f 9 15*f 9 15*f 9
  //   15*f 9 15*f 9 15*f 9 15*f 9 15*f 9 15*f 9 15*f 9 15*f 9 15*f 9 15*f 9 15*f 9 15*f 9 15*f 9 15*f 9
  //   15*f b d 14*f b d 14*f b d 14*f b d 14*f 9 15*f 9 15*f 9 15*f 9 15*f 9 15*f 9 15*f 9 15*f 9 15*f 9
  //   15*f 9 15*f 9 15*f 9 15*f b d 14*f b d 14*f b d 14*f b d 14*f 9 15*f 9 15*f 9 15*f 9 15*f 9 15*f 9
  //   15*f 9 15*f 9 15*f 9 15*f 9 15*f 9 15*f 9 15*f b d 14*f b d 14*f b d 14*f b d 14*f 9 15*f 9 15*f 9
  //   15*f 9 15*f 9 15*f 9 15*f 9 15*f 9 15*f 9 15*f 9 15*f 9 15*f 9 15*f b d 14*f 9 15*f 9 15*f 9 15*f d
  //   15*f d 15*f d 2f d 13*f d 8f d 13*f d 4f d 13*f d 1f d 13*f d d 2f d 12*f d d 8f d 12*f d d 2f d
  //   12*f d d 1f d 13*f e d d 1f d 13*f 1f d 11*f 5 15*f
  //   contents of EEPROM5 (hex, n*v repeats v):
  //   74 15*76 70 15*76 36 74 14*76 36 74 14*76 36 74 14*76 36 74 14*76 36 74 14*76 36 74 14*76 74 15*76
  //   74 15*76 74 15*76 74 15*76 74 15*76 74 15*76 74 15*76 74 15*76 74 15*76 74 15*76 74 15*76 74 15*76
  //   74 15*76 74 15*76 36 7c 14*76 36 7c 14*76 36 7c 14*76 36 7c 14*76 36 7c 14*76 36 7c 14*76 36 7c
  //   14*76 36 7c 14*76 36 3e 74 14*76 7c 15*76 7c 15*76 7c 15*76 7c 15*76 7c 15*76 7c 15*76 7c 15*76 7c
  //   15*76 3e 74 13*76 36 76 74 13*76 36 76 74 13*76 36 76 74 13*76 36 76 74 13*76 36 76 74 13*76 36 76
  //   74 13*76 36 76 74 13*76 36 76 74 13*76 36 76 36 74 14*76 74 15*76 74 15*76 74 15*76 74 15*76 74
  //   15*76 74 15*76 74 15*76 74 15*76 36 74 12*76 36 36 74 13*76 36 36 74 13*76 36 36 74 13*76 36 36 74
  //   13*76 36 36 74 13*76 36 36 74 13*76 36 36 74 13*76 36 36 74 13*76 36 36 36 74 12*76 66 74 14*76 66
  //   74 14*76 66 74 14*76 66 74 14*76 36 7e 66 74 13*76 7e 66 74 12*76 36 76 76 66 74 14*76 66 74 11*76
  //   36 76 76 66 74 11*76 26 74 15*76 54 15*76 54 15*76 54 15*76 54 14*76 36 56 7c 14*76 56 7c 13*76 36
  //   76 56 74 14*76 56 74 12*76 36 76 56 74 13*76 74 15*76 74 15*76 74 15*76 74 14*76 74 15*76 74 15*76
  //   74 15*76 74 15*76 74 15*76 74 15*76 74 15*76 74 15*76 74 15*76 74 15*76 74 15*76 74 16*76 74 15*76
  //   74 15*76 74 15*76 74 14*76 74 15*76 74 15*76 74 15*76 74 15*76 74 15*76 74 15*76 74 15*76 74 15*76
  //   74 15*76 74 15*76 74 15*76 74 15*76 74 15*76 74 15*76 74 15*76 74 15*76 74 15*76 74 15*76 74 15*76
  //   74 15*76 74 15*76 74 15*76 74 15*76 74 15*76 74 15*76 74 15*76 74 15*76 74 16*76 74 15*76 74 15*76
  //   74 15*76 74 14*76 74 15*76 74 15*76 74 15*76 74 15*76 74 15*76 74 15*76 74 15*76 74 15*76 74 15*76
  //   74 15*76 74 15*76 74 16*76 74 15*76 74 15*76 74 15*76 74 14*76 74 15*76 74 15*76 74 15*76 74 15*76
  //   74 15*76 74 15*76 74 15*76 74 15*76 74 15*76 74 15*76 74 15*76 74 16*76 74 15*76 74 15*76 74 15*76
  //   74 14*76 74 15*76 74 15*76 74 15*76 74 15*76 74 15*76 74 15*76 74 15*76 74 15*76 74 15*76 74 15*76
  //   74 15*76 74 16*76 74 14*76 74 15*76 74 15*76 74 15*76 74 15*76 74 15*76 36 76 74 13*76 36 76 74
  //   13*76 36 76 74 13*76 36 76 74 13*76 36 36 76 74 12*76 36 36 76 74 12*76 36 36 76 74 12*76 36 36 76
  //   74 12*76 66 66 36 36 76 74 11*76 56 56 76 74 11*76 74 15*76
  //   contents of EEPROM6 (hex, n*v repeats v):
  //   32*1 0 15*1 0 15*1 0 15*1 0 15*1 0 15*1 0 239*1 0 15*1 0 15*1 0 15*1 0 15*1 0 15*1 0 15*1 0 15*1 0
  //   15*1 0 0 143*1 0 14*1 0 15*1 0 15*1 0 15*1 0 15*1 0 15*1 0 15*1 0 15*1 0 15*1 0 1 0 143*1 0 13*1 0 0
  //   14*1 0 0 14*1 0 0 14*1 0 0 14*1 0 0 14*1 0 0 14*1 0 0 14*1 0 0 14*1 0 0 0 13*1
endmodule

module AddrDecoder (
  input  [15:0] ABUS,
  output NOT_DEVICE_SEL_ROM,
  output NOT_DEVICE_SEL_RAM
);

  wire decoder_1_out0, decoder_1_out1;

  Decoder #(.select(3)) decoder_1 (
    .out0(decoder_1_out0), .out1(decoder_1_out1), .sel(ABUS[15:13]), .en(1'b1));  // open: out2, out3, out4, out5, out6, out7
  not not_1 (NOT_DEVICE_SEL_ROM, decoder_1_out0);
  not not_2 (NOT_DEVICE_SEL_RAM, decoder_1_out1);
endmodule
